// Logisim project ALU.circ as structural Verilog
module HalfAdder (
  input  a,
  input  b,
  output sum,
  output carry
);

  xor XOR (sum, a, b);
  and OX (carry, a, b);

  // Notes on the sheet:
  //   Half Adder
endmodule

module FullAdder (
  input  a,
  input  b,
  input  c,
  output sum,
  output carry
);

  wire HalfAdder_2_carry, HalfAdder_carry, HalfAdder_sum;

  HalfAdder HalfAdder (.a(a), .b(b), .sum(HalfAdder_sum), .carry(HalfAdder_carry));
  HalfAdder HalfAdder_2 (.a(HalfAdder_sum), .b(c), .sum(sum), .carry(HalfAdder_2_carry));
  or or_1 (carry, HalfAdder_carry, HalfAdder_2_carry);

  // Notes on the sheet:
  //   FullAdder
endmodule

module Add16 (
  input  [15:0] In_A,
  input  [15:0] In_B,
  output [15:0] Out
);

  wire FullAdder_2_carry, FullAdder_3_carry, FullAdder_4_carry, FullAdder_5_carry, FullAdder_6_carry,
       FullAdder_7_carry, FullAdder_8_carry, FullAdder_9_carry, FullAdder_10_carry, FullAdder_11_carry,
       FullAdder_12_carry, FullAdder_13_carry, FullAdder_14_carry, FullAdder_carry, HalfAdder_carry;

  HalfAdder HalfAdder (.a(In_A[0]), .b(In_B[0]), .sum(Out[0]), .carry(HalfAdder_carry));
  FullAdder FullAdder (.a(In_A[1]), .b(In_B[1]), .c(HalfAdder_carry), .sum(Out[1]), .carry(FullAdder_carry));
  FullAdder FullAdder_2 (.a(In_A[2]), .b(In_B[2]), .c(FullAdder_carry), .sum(Out[2]), .carry(FullAdder_2_carry));
  FullAdder FullAdder_3 (.a(In_A[3]), .b(In_B[3]), .c(FullAdder_2_carry), .sum(Out[3]), .carry(FullAdder_3_carry));
  FullAdder FullAdder_4 (.a(In_A[4]), .b(In_B[4]), .c(FullAdder_3_carry), .sum(Out[4]), .carry(FullAdder_4_carry));
  FullAdder FullAdder_5 (.a(In_A[5]), .b(In_B[5]), .c(FullAdder_4_carry), .sum(Out[5]), .carry(FullAdder_5_carry));
  FullAdder FullAdder_6 (.a(In_A[6]), .b(In_B[6]), .c(FullAdder_5_carry), .sum(Out[6]), .carry(FullAdder_6_carry));
  FullAdder FullAdder_7 (.a(In_A[7]), .b(In_B[7]), .c(FullAdder_6_carry), .sum(Out[7]), .carry(FullAdder_7_carry));
  FullAdder FullAdder_8 (.a(In_A[8]), .b(In_B[8]), .c(FullAdder_7_carry), .sum(Out[8]), .carry(FullAdder_8_carry));
  FullAdder FullAdder_9 (.a(In_A[9]), .b(In_B[9]), .c(FullAdder_8_carry), .sum(Out[9]), .carry(FullAdder_9_carry));
  FullAdder FullAdder_10 (.a(In_A[10]), .b(In_B[10]), .c(FullAdder_9_carry), .sum(Out[10]), .carry(FullAdder_10_carry));
  FullAdder FullAdder_11 (
    .a(In_A[11]), .b(In_B[11]), .c(FullAdder_10_carry), .sum(Out[11]), .carry(FullAdder_11_carry));
  FullAdder FullAdder_12 (
    .a(In_A[12]), .b(In_B[12]), .c(FullAdder_11_carry), .sum(Out[12]), .carry(FullAdder_12_carry));
  FullAdder FullAdder_13 (
    .a(In_A[13]), .b(In_B[13]), .c(FullAdder_12_carry), .sum(Out[13]), .carry(FullAdder_13_carry));
  FullAdder FullAdder_14 (
    .a(In_A[14]), .b(In_B[14]), .c(FullAdder_13_carry), .sum(Out[14]), .carry(FullAdder_14_carry));
  FullAdder FullAdder_15 (.a(In_A[15]), .b(In_B[15]), .c(FullAdder_14_carry), .sum(Out[15]));  // open: carry
endmodule
